# Fritzing sketch Classic Controller to USB Adapter (saved by Fritzing 0.9.1b)
circuit board: 8.46667cm x 5.64444cm

parts:
  Part1 = Arduino Micro (Rev3)
  X1 = DB9 Connector [package=db9]
  X2 = DB9 Connector [package=db9]
  X3 = DB9 Connector [package=db9]
  S1 = Round Pushbutton
  R1 = Resistor [tolerance=±5% resistance=330 package=THT]
  R2 = Resistor [tolerance=±5% resistance=330 package=THT]
  R3 = Resistor [tolerance=±5% resistance=330 package=THT]
  LED1 = LED - 5mm [color="Red (633nm)" package="5 mm [THT]"]
  LED2 = LED - 5mm [color="Yellow (595nm)" package="5 mm [THT]"]
  LED3 = LED - 5mm [color="Green (570nm)" package="5 mm [THT]"]

nets:
  N1: Part1.GND, S1.leg1, LED1.cathode, LED2.cathode, LED3.cathode
  N2: Part1.D2/SDA, X1.1, X2.1, X3.1
  N3: Part1.D3/SCL, X1.2, X2.2, X3.2
  N4: Part1.D4_PWM/A6, X1.3, X2.3, X3.3
  N5: Part1.D5_PWM, X1.4, X2.4, X3.4
  N6: Part1.D6_PWM/A7, X1.6, X2.6, X3.6
  N7: Part1.D7, X1.7, X2.7, X3.7
  N8: Part1.D8_PWM/A8, X1.9, X2.9, X3.9
  N9: Part1.D9_PWM/A9, S1.leg0
  N10: Part1.D10_PWM/A10, R1.Pin_1
  N11: Part1.D11_PWM, R2.Pin_1
  N12: Part1.D12_PWM/A11, R3.Pin_1
  N13: Part1.A5, X3.8
  N14: Part1.A4, X3.5
  N15: Part1.A3, X2.8
  N16: Part1.A2, X2.5
  N17: Part1.A1, X1.8
  N18: Part1.A0, X1.5
  N19: R1.Pin_0, LED1.anode
  N20: R2.Pin_0, LED2.anode
  N21: R3.Pin_0, LED3.anode
